# Fritzing sketch amp (saved by Fritzing 0.9.10b)

parts:
  Part1 = Adafruit MAX9744 20W Amplifier [part_number="Adafruit #1752"]
  Mod1 = Raspberry Pi Pico
  RE1 = Rotary Encoder [package=THT]
  Mod3 = generic-ac-power-supply [package=THT]
  Part2 = 24 NeoPixel Ring [part_number=1586]

nets:
  N1: Part1.GND, Part1.SCL, Part1.VI2C, Mod1.pin_3, Mod1.pin_33, Mod1.pin_38, RE1.SwitchrPinD, Mod3.pin3#3
  N2: Part1.SDA, Mod1.pin_32
  N3: Part1.MUTE, Part1.SYNCOUT, Mod1.pin_30
  N4: Mod1.pin_1, RE1.EncoderPinA
  N5: Mod1.pin_2, RE1.EncoderPinC
  N6: Mod1.pin_4, RE1.EncoderPinB
  N7: Mod1.pin_34, Part2.IN
  N8: Mod1.pin_37, RE1.SwitchPinE
  N9: Mod1.pin_39, Mod3.pin3#2, Part2.VDD

custom parts:
  Adafruit MAX9744 20W Amplifier: Pump up the volume with this 20W stereo amplifier! This slim little board has a class D amplifier onboard that can drive 2 channels of 4-8 ohm impedance speakers at 20W each. Power it with 5-12VDC using the onboard DC power jack and plug stereo line level into the 3.5mm stereo headphone jack and jam out with ease. Since it's class D, its completely cool-running, no heat sinks are required and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
  Raspberry Pi Pico: Raspberry Pi Pico. Based around the RP2040 microcontroller the Pico is a low cost microcontroller device bringing Raspberry Pi quality, cost, and easy of use to the microcontroller space. Jan 2021, Split part in to two versions: SMD (this one) and tht. This one is single sided and uses the castellation pads to solder the module to the board (no holes, other than for the USB connector!). The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
  Rotary Encoder: Rotary Encoder from ALPSec11e with switch.
  generic-ac-power-supply: Generic ac power supply module. Use as is, or customize the svgs to fit your particular device (as they are all different.) Provides AC input and single DC output. PCB is generic and will need modifications if you intend to do a pcb mount.
  24 NeoPixel Ring: 24 ultra bright smart LED NeoPixels are arranged in a circle with 2.6" (66mm) outer diameter. The rings are 'chainable' - connect the output pin of one to the input pin of another. Use only one microcontroller pin to control as many as you can chain together! Each LED is addressable as the driver chip is inside the LED. Each one has ~18mA constant current drive so the color will be very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
